# Fritzing sketch Arduino Uno (Rev3) + Keypad 4x3 + 1602 LCD + I2C Module Connection (saved by Fritzing 0.9.4)
breadboards: 1

parts:
  Onderdeel2 = Arduino Uno (Rev3)
  LCD2 = LCD screen
  LCM1602_IIC2 = LCM1602 IIC [part_number="LCM1602 IIC" chip_label="LCM1602 IIC" package="DIP (Dual Inline) [THT]"]
  kEYPAD_MATRICIAL_1 = KEYPAD 4x3

nets:
  N1: Onderdeel2.A4/SDA, LCM1602_IIC2.SDA
  N2: Onderdeel2.D8, kEYPAD_MATRICIAL_1.arrow1
  N3: Onderdeel2.D9_PWM, kEYPAD_MATRICIAL_1.col1
  N4: Onderdeel2.A5/SCL, LCM1602_IIC2.SCL
  N5: Onderdeel2.D3_PWM, kEYPAD_MATRICIAL_1.arrow4
  N6: Onderdeel2.D4, kEYPAD_MATRICIAL_1.arrow3
  N7: Onderdeel2.D5_PWM, kEYPAD_MATRICIAL_1.col3
  N8: Onderdeel2.D6_PWM, kEYPAD_MATRICIAL_1.arrow2
  N9: Onderdeel2.D7, kEYPAD_MATRICIAL_1.col2
  5V: Onderdeel2.5V, LCM1602_IIC2.VCC
  GND: Onderdeel2.GND, LCM1602_IIC2.GND
  VSS: LCD2.VSS, LCM1602_IIC2.VSS
  VDD: LCD2.VDD, LCM1602_IIC2.VDD
  N10: LCD2.V0, LCM1602_IIC2.V0
  N11: LCD2.RS, LCM1602_IIC2.RS
  N12: LCD2.R/W, LCM1602_IIC2.RW
  N13: LCD2.E, LCM1602_IIC2.E
  N14: LCD2.DB0, LCM1602_IIC2.D0
  N15: LCD2.DB1, LCM1602_IIC2.D1
  N16: LCD2.DB2, LCM1602_IIC2.D2
  N17: LCD2.DB3, LCM1602_IIC2.D3
  N18: LCD2.DB4, LCM1602_IIC2.D4
  N19: LCD2.DB5, LCM1602_IIC2.D5
  N20: LCD2.DB6, LCM1602_IIC2.D6
  N21: LCD2.DB7, LCM1602_IIC2.D7
  N22: LCD2.LED+, LCM1602_IIC2.A
  N23: LCD2.LED-, LCM1602_IIC2.K
  N24: LCM1602_IIC2.LED_A, LCM1602_IIC2.LED_B

custom parts:
  LCM1602 IIC: I2C-Module to use a 1602 or 2004 LCD on with the wire.h libory Serial LCD Modul
  KEYPAD 4x3: KEYPAD matricial de 12 botones, 4 filas x 3 columnas
